// Digital circuit registrador 32 bits.dig as structural Verilog
module registrador_32_bits (
  input  [31:0] in_1,
  input  clk,
  input  [4:0] in_4,
  input  in_5,
  output [31:0] out_3
);

  wire demultiplexer_1_out_0, demultiplexer_1_out_1, demultiplexer_1_out_2, demultiplexer_1_out_3,
       demultiplexer_1_out_4, demultiplexer_1_out_5, demultiplexer_1_out_6, demultiplexer_1_out_7,
       demultiplexer_1_out_8, demultiplexer_1_out_9, demultiplexer_1_out_10, demultiplexer_1_out_11,
       demultiplexer_1_out_12, demultiplexer_1_out_13, demultiplexer_1_out_14, demultiplexer_1_out_15,
       demultiplexer_1_out_16, demultiplexer_1_out_17, demultiplexer_1_out_18, demultiplexer_1_out_19,
       demultiplexer_1_out_20, demultiplexer_1_out_21, demultiplexer_1_out_22, demultiplexer_1_out_23,
       demultiplexer_1_out_24, demultiplexer_1_out_25, demultiplexer_1_out_26, demultiplexer_1_out_27,
       demultiplexer_1_out_28, demultiplexer_1_out_29, demultiplexer_1_out_30, demultiplexer_1_out_31;
  wire [4:0] demultiplexer_2_out_0, demultiplexer_2_out_1;
  wire [31:0] d_ff_1_q, d_ff_2_q, d_ff_3_q, d_ff_4_q, d_ff_5_q, d_ff_6_q, d_ff_7_q, d_ff_8_q, d_ff_9_q,
       d_ff_10_q, d_ff_11_q, d_ff_12_q, d_ff_13_q, d_ff_14_q, d_ff_15_q, d_ff_16_q, d_ff_17_q, d_ff_18_q,
       d_ff_19_q, d_ff_20_q, d_ff_21_q, d_ff_22_q, d_ff_23_q, d_ff_24_q, d_ff_25_q, d_ff_26_q, d_ff_27_q,
       d_ff_28_q, d_ff_29_q, d_ff_30_q, d_ff_31_q, d_ff_32_q, multiplexer_1_out, multiplexer_2_out,
       multiplexer_3_out, multiplexer_4_out, multiplexer_5_out, multiplexer_6_out, multiplexer_7_out,
       multiplexer_8_out, multiplexer_9_out, multiplexer_10_out, multiplexer_11_out, multiplexer_12_out,
       multiplexer_13_out, multiplexer_14_out, multiplexer_15_out, multiplexer_16_out, multiplexer_17_out,
       multiplexer_18_out, multiplexer_19_out, multiplexer_20_out, multiplexer_21_out, multiplexer_22_out,
       multiplexer_23_out, multiplexer_24_out, multiplexer_25_out, multiplexer_26_out, multiplexer_27_out,
       multiplexer_28_out, multiplexer_29_out, multiplexer_30_out, multiplexer_31_out, multiplexer_32_out;

  Demultiplexer #(.Selector_Bits(5)) demultiplexer_1 (
    .sel(demultiplexer_2_out_1), .in(1'b1), .out_0(demultiplexer_1_out_0), .out_1(demultiplexer_1_out_1),
    .out_2(demultiplexer_1_out_2), .out_3(demultiplexer_1_out_3), .out_4(demultiplexer_1_out_4),
    .out_5(demultiplexer_1_out_5), .out_6(demultiplexer_1_out_6), .out_7(demultiplexer_1_out_7),
    .out_8(demultiplexer_1_out_8), .out_9(demultiplexer_1_out_9), .out_10(demultiplexer_1_out_10),
    .out_11(demultiplexer_1_out_11), .out_12(demultiplexer_1_out_12), .out_13(demultiplexer_1_out_13),
    .out_14(demultiplexer_1_out_14), .out_15(demultiplexer_1_out_15), .out_16(demultiplexer_1_out_16),
    .out_17(demultiplexer_1_out_17), .out_18(demultiplexer_1_out_18), .out_19(demultiplexer_1_out_19),
    .out_20(demultiplexer_1_out_20), .out_21(demultiplexer_1_out_21), .out_22(demultiplexer_1_out_22),
    .out_23(demultiplexer_1_out_23), .out_24(demultiplexer_1_out_24), .out_25(demultiplexer_1_out_25),
    .out_26(demultiplexer_1_out_26), .out_27(demultiplexer_1_out_27), .out_28(demultiplexer_1_out_28),
    .out_29(demultiplexer_1_out_29), .out_30(demultiplexer_1_out_30), .out_31(demultiplexer_1_out_31));
  Multiplexer #(.Bits(32)) multiplexer_1 (
    .sel(demultiplexer_1_out_0), .in_0(multiplexer_1_out), .in_1(in_1), .out(multiplexer_1_out));
  D_FF #(.Bits(32)) d_ff_1 (.D(multiplexer_1_out), .C(clk), .Q(d_ff_1_q));  // open: nQ
  Multiplexer #(.Bits(32)) multiplexer_2 (
    .sel(demultiplexer_1_out_8), .in_0(multiplexer_2_out), .in_1(in_1), .out(multiplexer_2_out));
  D_FF #(.Bits(32)) d_ff_2 (.D(multiplexer_2_out), .C(clk), .Q(d_ff_2_q));  // open: nQ
  Multiplexer #(.Bits(32)) multiplexer_3 (
    .sel(demultiplexer_1_out_16), .in_0(multiplexer_3_out), .in_1(in_1), .out(multiplexer_3_out));
  D_FF #(.Bits(32)) d_ff_3 (.D(multiplexer_3_out), .C(clk), .Q(d_ff_3_q));  // open: nQ
  Multiplexer #(.Bits(32)) multiplexer_4 (
    .sel(demultiplexer_1_out_24), .in_0(multiplexer_4_out), .in_1(in_1), .out(multiplexer_4_out));
  D_FF #(.Bits(32)) d_ff_4 (.D(multiplexer_4_out), .C(clk), .Q(d_ff_4_q));  // open: nQ
  D_FF #(.Bits(32)) d_ff_5 (.D(multiplexer_5_out), .C(clk), .Q(d_ff_5_q));  // open: nQ
  D_FF #(.Bits(32)) d_ff_6 (.D(multiplexer_6_out), .C(clk), .Q(d_ff_6_q));  // open: nQ
  D_FF #(.Bits(32)) d_ff_7 (.D(multiplexer_7_out), .C(clk), .Q(d_ff_7_q));  // open: nQ
  D_FF #(.Bits(32)) d_ff_8 (.D(multiplexer_8_out), .C(clk), .Q(d_ff_8_q));  // open: nQ
  Multiplexer #(.Bits(32)) multiplexer_5 (
    .sel(demultiplexer_1_out_1), .in_0(multiplexer_5_out), .in_1(in_1), .out(multiplexer_5_out));
  Multiplexer #(.Bits(32)) multiplexer_6 (
    .sel(demultiplexer_1_out_9), .in_0(multiplexer_6_out), .in_1(in_1), .out(multiplexer_6_out));
  Multiplexer #(.Bits(32)) multiplexer_7 (
    .sel(demultiplexer_1_out_17), .in_0(multiplexer_7_out), .in_1(in_1), .out(multiplexer_7_out));
  Multiplexer #(.Bits(32)) multiplexer_8 (
    .sel(demultiplexer_1_out_25), .in_0(multiplexer_8_out), .in_1(in_1), .out(multiplexer_8_out));
  D_FF #(.Bits(32)) d_ff_9 (.D(multiplexer_9_out), .C(clk), .Q(d_ff_9_q));  // open: nQ
  D_FF #(.Bits(32)) d_ff_10 (.D(multiplexer_10_out), .C(clk), .Q(d_ff_10_q));  // open: nQ
  D_FF #(.Bits(32)) d_ff_11 (.D(multiplexer_11_out), .C(clk), .Q(d_ff_11_q));  // open: nQ
  D_FF #(.Bits(32)) d_ff_12 (.D(multiplexer_12_out), .C(clk), .Q(d_ff_12_q));  // open: nQ
  Multiplexer #(.Bits(32)) multiplexer_9 (
    .sel(demultiplexer_1_out_2), .in_0(multiplexer_9_out), .in_1(in_1), .out(multiplexer_9_out));
  Multiplexer #(.Bits(32)) multiplexer_10 (
    .sel(demultiplexer_1_out_10), .in_0(multiplexer_10_out), .in_1(in_1), .out(multiplexer_10_out));
  Multiplexer #(.Bits(32)) multiplexer_11 (
    .sel(demultiplexer_1_out_18), .in_0(multiplexer_11_out), .in_1(in_1), .out(multiplexer_11_out));
  Multiplexer #(.Bits(32)) multiplexer_12 (
    .sel(demultiplexer_1_out_26), .in_0(multiplexer_12_out), .in_1(in_1), .out(multiplexer_12_out));
  Demultiplexer #(.Bits(5)) demultiplexer_2 (
    .sel(in_5), .in(in_4), .out_0(demultiplexer_2_out_0), .out_1(demultiplexer_2_out_1));
  Multiplexer #(.Bits(32)) multiplexer_13 (
    .sel(demultiplexer_1_out_3), .in_0(multiplexer_13_out), .in_1(in_1), .out(multiplexer_13_out));
  D_FF #(.Bits(32)) d_ff_13 (.D(multiplexer_13_out), .C(clk), .Q(d_ff_13_q));  // open: nQ
  Multiplexer #(.Bits(32)) multiplexer_14 (
    .sel(demultiplexer_1_out_11), .in_0(multiplexer_14_out), .in_1(in_1), .out(multiplexer_14_out));
  D_FF #(.Bits(32)) d_ff_14 (.D(multiplexer_14_out), .C(clk), .Q(d_ff_14_q));  // open: nQ
  Multiplexer #(.Bits(32)) multiplexer_15 (
    .sel(demultiplexer_1_out_19), .in_0(multiplexer_15_out), .in_1(in_1), .out(multiplexer_15_out));
  D_FF #(.Bits(32)) d_ff_15 (.D(multiplexer_15_out), .C(clk), .Q(d_ff_15_q));  // open: nQ
  Multiplexer #(.Bits(32)) multiplexer_16 (
    .sel(demultiplexer_1_out_27), .in_0(multiplexer_16_out), .in_1(in_1), .out(multiplexer_16_out));
  D_FF #(.Bits(32)) d_ff_16 (.D(multiplexer_16_out), .C(clk), .Q(d_ff_16_q));  // open: nQ
  Multiplexer #(.Bits(32)) multiplexer_17 (
    .sel(demultiplexer_1_out_4), .in_0(multiplexer_17_out), .in_1(in_1), .out(multiplexer_17_out));
  D_FF #(.Bits(32)) d_ff_17 (.D(multiplexer_17_out), .C(clk), .Q(d_ff_17_q));  // open: nQ
  Multiplexer #(.Bits(32)) multiplexer_18 (
    .sel(demultiplexer_1_out_12), .in_0(multiplexer_18_out), .in_1(in_1), .out(multiplexer_18_out));
  D_FF #(.Bits(32)) d_ff_18 (.D(multiplexer_18_out), .C(clk), .Q(d_ff_18_q));  // open: nQ
  Multiplexer #(.Bits(32)) multiplexer_19 (
    .sel(demultiplexer_1_out_20), .in_0(multiplexer_19_out), .in_1(in_1), .out(multiplexer_19_out));
  D_FF #(.Bits(32)) d_ff_19 (.D(multiplexer_19_out), .C(clk), .Q(d_ff_19_q));  // open: nQ
  Multiplexer #(.Bits(32)) multiplexer_20 (
    .sel(demultiplexer_1_out_28), .in_0(multiplexer_20_out), .in_1(in_1), .out(multiplexer_20_out));
  D_FF #(.Bits(32)) d_ff_20 (.D(multiplexer_20_out), .C(clk), .Q(d_ff_20_q));  // open: nQ
  D_FF #(.Bits(32)) d_ff_21 (.D(multiplexer_21_out), .C(clk), .Q(d_ff_21_q));  // open: nQ
  D_FF #(.Bits(32)) d_ff_22 (.D(multiplexer_22_out), .C(clk), .Q(d_ff_22_q));  // open: nQ
  D_FF #(.Bits(32)) d_ff_23 (.D(multiplexer_23_out), .C(clk), .Q(d_ff_23_q));  // open: nQ
  D_FF #(.Bits(32)) d_ff_24 (.D(multiplexer_24_out), .C(clk), .Q(d_ff_24_q));  // open: nQ
  Multiplexer #(.Bits(32)) multiplexer_21 (
    .sel(demultiplexer_1_out_5), .in_0(multiplexer_21_out), .in_1(in_1), .out(multiplexer_21_out));
  Multiplexer #(.Bits(32)) multiplexer_22 (
    .sel(demultiplexer_1_out_13), .in_0(multiplexer_22_out), .in_1(in_1), .out(multiplexer_22_out));
  Multiplexer #(.Bits(32)) multiplexer_23 (
    .sel(demultiplexer_1_out_21), .in_0(multiplexer_23_out), .in_1(in_1), .out(multiplexer_23_out));
  Multiplexer #(.Bits(32)) multiplexer_24 (
    .sel(demultiplexer_1_out_29), .in_0(multiplexer_24_out), .in_1(in_1), .out(multiplexer_24_out));
  D_FF #(.Bits(32)) d_ff_25 (.D(multiplexer_25_out), .C(clk), .Q(d_ff_25_q));  // open: nQ
  D_FF #(.Bits(32)) d_ff_26 (.D(multiplexer_26_out), .C(clk), .Q(d_ff_26_q));  // open: nQ
  D_FF #(.Bits(32)) d_ff_27 (.D(multiplexer_27_out), .C(clk), .Q(d_ff_27_q));  // open: nQ
  D_FF #(.Bits(32)) d_ff_28 (.D(multiplexer_28_out), .C(clk), .Q(d_ff_28_q));  // open: nQ
  Multiplexer #(.Bits(32)) multiplexer_25 (
    .sel(demultiplexer_1_out_6), .in_0(multiplexer_25_out), .in_1(in_1), .out(multiplexer_25_out));
  Multiplexer #(.Bits(32)) multiplexer_26 (
    .sel(demultiplexer_1_out_14), .in_0(multiplexer_26_out), .in_1(in_1), .out(multiplexer_26_out));
  Multiplexer #(.Bits(32)) multiplexer_27 (
    .sel(demultiplexer_1_out_22), .in_0(multiplexer_27_out), .in_1(in_1), .out(multiplexer_27_out));
  Multiplexer #(.Bits(32)) multiplexer_28 (
    .sel(demultiplexer_1_out_30), .in_0(multiplexer_28_out), .in_1(in_1), .out(multiplexer_28_out));
  Multiplexer #(.Bits(32)) multiplexer_29 (
    .sel(demultiplexer_1_out_7), .in_0(multiplexer_29_out), .in_1(in_1), .out(multiplexer_29_out));
  D_FF #(.Bits(32)) d_ff_29 (.D(multiplexer_29_out), .C(clk), .Q(d_ff_29_q));  // open: nQ
  Multiplexer #(.Bits(32)) multiplexer_30 (
    .sel(demultiplexer_1_out_15), .in_0(multiplexer_30_out), .in_1(in_1), .out(multiplexer_30_out));
  D_FF #(.Bits(32)) d_ff_30 (.D(multiplexer_30_out), .C(clk), .Q(d_ff_30_q));  // open: nQ
  Multiplexer #(.Bits(32)) multiplexer_31 (
    .sel(demultiplexer_1_out_23), .in_0(multiplexer_31_out), .in_1(in_1), .out(multiplexer_31_out));
  D_FF #(.Bits(32)) d_ff_31 (.D(multiplexer_31_out), .C(clk), .Q(d_ff_31_q));  // open: nQ
  Multiplexer #(.Bits(32)) multiplexer_32 (
    .sel(demultiplexer_1_out_31), .in_0(multiplexer_32_out), .in_1(in_1), .out(multiplexer_32_out));
  D_FF #(.Bits(32)) d_ff_32 (.D(multiplexer_32_out), .C(clk), .Q(d_ff_32_q));  // open: nQ
  Multiplexer #(.Bits(32), .Selector_Bits(5)) multiplexer_33 (
    .sel(demultiplexer_2_out_0), .in_0(d_ff_1_q), .in_1(d_ff_5_q), .in_2(d_ff_9_q), .in_3(d_ff_13_q),
    .in_4(d_ff_17_q), .in_5(d_ff_21_q), .in_6(d_ff_25_q), .in_7(d_ff_29_q), .in_8(d_ff_2_q), .in_9(d_ff_6_q),
    .in_10(d_ff_10_q), .in_11(d_ff_14_q), .in_12(d_ff_18_q), .in_13(d_ff_22_q), .in_14(d_ff_26_q),
    .in_15(d_ff_30_q), .in_16(d_ff_3_q), .in_17(d_ff_7_q), .in_18(d_ff_11_q), .in_19(d_ff_15_q),
    .in_20(d_ff_19_q), .in_21(d_ff_23_q), .in_22(d_ff_27_q), .in_23(d_ff_31_q), .in_24(d_ff_4_q),
    .in_25(d_ff_8_q), .in_26(d_ff_12_q), .in_27(d_ff_16_q), .in_28(d_ff_20_q), .in_29(d_ff_24_q),
    .in_30(d_ff_28_q), .in_31(d_ff_32_q), .out(out_3));
endmodule
