// Digital circuit regs.dig as structural Verilog
module regs (
  input  [31:0] C,
  input  clk,
  input  [3:0] c_2,
  input  [3:0] a,
  input  [3:0] b,
  input  wr,
  output [31:0] B_2,
  output [31:0] A_2
);

  wire and_1_out, demultiplexer_1_out_1, demultiplexer_1_out_2, demultiplexer_1_out_3, demultiplexer_1_out_4,
       demultiplexer_1_out_5, demultiplexer_1_out_6, demultiplexer_1_out_7, demultiplexer_1_out_8,
       demultiplexer_1_out_9, demultiplexer_1_out_10, demultiplexer_1_out_11, demultiplexer_1_out_12,
       demultiplexer_1_out_13, demultiplexer_1_out_14, demultiplexer_1_out_15;
  wire [31:0] multiplexer_1_out, multiplexer_2_out, multiplexer_3_out, multiplexer_4_out, multiplexer_5_out,
       multiplexer_6_out, multiplexer_7_out, multiplexer_8_out, multiplexer_9_out, multiplexer_11_out,
       multiplexer_12_out, multiplexer_13_out, multiplexer_14_out, multiplexer_16_out, multiplexer_17_out,
       multiplexer_18_out, r0_q, r1_q, r2_q, r3_q, r4_q, r5_q, r6_q, r7_q, r8_q, r9_q, r10_q, r11_q, r12_q,
       r13_q, r14_q, r15_q;

  Multiplexer #(.Bits(32)) multiplexer_1 (
    .sel(demultiplexer_1_out_15), .in_0(r15_q), .in_1(C), .out(multiplexer_1_out));
  Register #(.Bits(32)) r15 (.D(multiplexer_1_out), .C(clk), .en(1'b1), .Q(r15_q));
  Multiplexer #(.Bits(32)) multiplexer_2 (
    .sel(demultiplexer_1_out_14), .in_0(r14_q), .in_1(C), .out(multiplexer_2_out));
  Register #(.Bits(32)) r14 (.D(multiplexer_2_out), .C(clk), .en(1'b1), .Q(r14_q));
  Multiplexer #(.Bits(32)) multiplexer_3 (
    .sel(demultiplexer_1_out_13), .in_0(r13_q), .in_1(C), .out(multiplexer_3_out));
  Register #(.Bits(32)) r13 (.D(multiplexer_3_out), .C(clk), .en(1'b1), .Q(r13_q));
  Register #(.Bits(32)) r12 (.D(multiplexer_4_out), .C(clk), .en(1'b1), .Q(r12_q));
  Multiplexer #(.Bits(32)) multiplexer_4 (
    .sel(demultiplexer_1_out_12), .in_0(r12_q), .in_1(C), .out(multiplexer_4_out));
  Multiplexer #(.Bits(32)) multiplexer_5 (
    .sel(demultiplexer_1_out_11), .in_0(r11_q), .in_1(C), .out(multiplexer_5_out));
  Register #(.Bits(32)) r11 (.D(multiplexer_5_out), .C(clk), .en(1'b1), .Q(r11_q));
  Multiplexer #(.Bits(32)) multiplexer_6 (
    .sel(demultiplexer_1_out_10), .in_0(r10_q), .in_1(C), .out(multiplexer_6_out));
  Register #(.Bits(32)) r10 (.D(multiplexer_6_out), .C(clk), .en(1'b1), .Q(r10_q));
  Multiplexer #(.Bits(32)) multiplexer_7 (.sel(demultiplexer_1_out_9), .in_0(r9_q), .in_1(C), .out(multiplexer_7_out));
  Register #(.Bits(32)) r9 (.D(multiplexer_7_out), .C(clk), .en(1'b1), .Q(r9_q));
  Register #(.Bits(32)) r8 (.D(multiplexer_8_out), .C(clk), .en(1'b1), .Q(r8_q));
  Multiplexer #(.Bits(32)) multiplexer_8 (.sel(demultiplexer_1_out_8), .in_0(r8_q), .in_1(C), .out(multiplexer_8_out));
  Multiplexer #(.Bits(32)) multiplexer_9 (.sel(demultiplexer_1_out_7), .in_0(r7_q), .in_1(C), .out(multiplexer_9_out));
  Register #(.Bits(32)) r7 (.D(multiplexer_9_out), .C(clk), .en(1'b1), .Q(r7_q));
  Multiplexer #(.Selector_Bits(4), .Bits(32)) multiplexer_10 (
    .sel(b), .in_0(r0_q), .in_1(r1_q), .in_2(r2_q), .in_3(r3_q), .in_4(r4_q), .in_5(r5_q), .in_6(r6_q),
    .in_7(r7_q), .in_8(r8_q), .in_9(r9_q), .in_10(r10_q), .in_11(r11_q), .in_12(r12_q), .in_13(r13_q),
    .in_14(r14_q), .in_15(r15_q), .out(B_2));
  Multiplexer #(.Bits(32)) multiplexer_11 (
    .sel(demultiplexer_1_out_6), .in_0(r6_q), .in_1(C), .out(multiplexer_11_out));
  Register #(.Bits(32)) r6 (.D(multiplexer_11_out), .C(clk), .en(1'b1), .Q(r6_q));
  Multiplexer #(.Bits(32)) multiplexer_12 (
    .sel(demultiplexer_1_out_5), .in_0(r5_q), .in_1(C), .out(multiplexer_12_out));
  Register #(.Bits(32)) r5 (.D(multiplexer_12_out), .C(clk), .en(1'b1), .Q(r5_q));
  Register #(.Bits(32)) r4 (.D(multiplexer_13_out), .C(clk), .en(1'b1), .Q(r4_q));
  Multiplexer #(.Bits(32)) multiplexer_13 (
    .sel(demultiplexer_1_out_4), .in_0(r4_q), .in_1(C), .out(multiplexer_13_out));
  Multiplexer #(.Bits(32)) multiplexer_14 (
    .sel(demultiplexer_1_out_3), .in_0(r3_q), .in_1(C), .out(multiplexer_14_out));
  Register #(.Bits(32)) r3 (.D(multiplexer_14_out), .C(clk), .en(1'b1), .Q(r3_q));
  Multiplexer #(.Selector_Bits(4), .Bits(32)) multiplexer_15 (
    .sel(a), .in_0(r0_q), .in_1(r1_q), .in_2(r2_q), .in_3(r3_q), .in_4(r4_q), .in_5(r5_q), .in_6(r6_q),
    .in_7(r7_q), .in_8(r8_q), .in_9(r9_q), .in_10(r10_q), .in_11(r11_q), .in_12(r12_q), .in_13(r13_q),
    .in_14(r14_q), .in_15(r15_q), .out(A_2));
  and and_1 (and_1_out, wr, 1'b1);
  Multiplexer #(.Bits(32)) multiplexer_16 (
    .sel(demultiplexer_1_out_2), .in_0(r2_q), .in_1(C), .out(multiplexer_16_out));
  Register #(.Bits(32)) r2 (.D(multiplexer_16_out), .C(clk), .en(1'b1), .Q(r2_q));
  Multiplexer #(.Bits(32)) multiplexer_17 (
    .sel(demultiplexer_1_out_1), .in_0(r1_q), .in_1(C), .out(multiplexer_17_out));
  Register #(.Bits(32)) r1 (.D(multiplexer_17_out), .C(clk), .en(1'b1), .Q(r1_q));
  Demultiplexer #(.Selector_Bits(4)) demultiplexer_1 (
    .sel(c_2), .in(and_1_out), .out_1(demultiplexer_1_out_1), .out_2(demultiplexer_1_out_2),
    .out_3(demultiplexer_1_out_3), .out_4(demultiplexer_1_out_4), .out_5(demultiplexer_1_out_5),
    .out_6(demultiplexer_1_out_6), .out_7(demultiplexer_1_out_7), .out_8(demultiplexer_1_out_8),
    .out_9(demultiplexer_1_out_9), .out_10(demultiplexer_1_out_10), .out_11(demultiplexer_1_out_11),
    .out_12(demultiplexer_1_out_12), .out_13(demultiplexer_1_out_13), .out_14(demultiplexer_1_out_14),
    .out_15(demultiplexer_1_out_15));  // open: out_0
  Register #(.Bits(32)) r0 (.D(multiplexer_18_out), .C(clk), .en(1'b1), .Q(r0_q));
  Multiplexer #(.Bits(32)) multiplexer_18 (.sel(1'b0), .in_0(r0_q), .in_1({32{1'b0}}), .out(multiplexer_18_out));
endmodule
