// Digital circuit MicoProcessador.dig as structural Verilog
module MicoProcessador (
  input  clk,
  output [15:0] ip,
  output Neg,
  output Overflow,
  output [31:0] S,
  output [31:0] Display
);

  wire [1:0] and_1_out, rom_2_d_2;
  wire [3:0] a, b, c, rom_1_d;
  wire [7:0] rom_2_d;
  wire [15:0] add_1_s, add_2_s, \const , multiplexer_1_out, regs_1_a_2;
  wire [31:0] bitextender_1_out, IP_plus_1_out, multiplexer_2_out, multiplexer_4_out, ramdualport_1_d,
       regs_1_b_2;
  wire [31:1] or_1_out;
  wire [31:16] regs_1_a_2_2;

  Register #(.Bits(16)) register_1 (.D(multiplexer_1_out), .C(clk), .en(1'b1), .Q(ip));
  Add #(.Bits(16)) add_1 (.a(ip), .b({16{1'b0}}), .c_i(1'b1), .s(add_1_s));  // open: c_o
  Multiplexer #(.Selector_Bits(2), .Bits(16)) multiplexer_1 (
    .sel(rom_2_d_2), .in_0(add_1_s), .in_1(ip), .in_2(\const ), .in_3(regs_1_a_2), .out(multiplexer_1_out));
  ROM #(.AddrBits(16), .Bits(32)) rom_1 (.A(ip), .sel(1'b1), .D({rom_1_d, a, b, c, \const }));
  regs regs_1 (
    .C(multiplexer_4_out), .clk(clk), .c_2(c), .a(a), .b(b), .wr(rom_2_d[7]), .B_2(regs_1_b_2),
    .A_2({regs_1_a_2_2, regs_1_a_2}));
  ROM #(.AddrBits(4), .Bits(10)) rom_2 (.A(rom_1_d), .sel(1'b1), .D({rom_2_d_2, rom_2_d}));
  BitExtender #(.inputBits(16), .outputBits(32)) bitextender_1 (.in(\const ), .out(bitextender_1_out));
  Multiplexer #(.Bits(32)) multiplexer_2 (
    .sel(rom_2_d[6]), .in_0(regs_1_b_2), .in_1(bitextender_1_out), .out(multiplexer_2_out));
  ULA2 ULA (.a({regs_1_a_2_2, regs_1_a_2}), .b(multiplexer_2_out), .over(Overflow), .S(S), .f(rom_2_d[2:0]));
  BitExtender #(.inputBits(16), .outputBits(32)) IP_plus_1 (.in(add_2_s), .out(IP_plus_1_out));
  Add #(.Bits(16)) add_2 (.a(ip), .b(16'h1), .c_i(1'b0), .s(add_2_s));  // open: c_o
  Multiplexer #(.Bits(32)) multiplexer_3 (
    .sel(and_1_out[0]), .in_0({32{1'b0}}), .in_1(multiplexer_4_out), .out(Display));
  Multiplexer #(.Selector_Bits(2), .Bits(32)) multiplexer_4 (
    .sel(rom_2_d[5:4]), .in_0(S), .in_1(ramdualport_1_d), .in_2(IP_plus_1_out),
    .in_3({regs_1_a_2_2, regs_1_a_2}), .out(multiplexer_4_out));
  RAMDualPort #(.AddrBits(16), .Bits(32)) ramdualport_1 (
    .A(ip), .Din(S), .str(rom_2_d[3]), .C(clk), .ld(1'b0), .D(ramdualport_1_d));
  assign and_1_out = rom_2_d[5:4] & 2'b11;  // And and_1, 2 bits wide
  assign {or_1_out, Neg} = S | 32'h80000000;  // Or or_1, 32 bits wide

  // Notes on the sheet:
  //   contents of rom_1 (hex, n*v repeats v):
  //   8001000e,80020004,1230000,11230000,21230000,31230000,41230000
  //   ,51230000,61230000,71230000,a2400000,82040000,b2000000,f0000000
  //   contents of rom_2 (hex, n*v repeats v):
  //   80,81,82,83,84,85,86,87,c0,d0,48,30,2a0,2a0,300,186
endmodule
