// Digital circuit ULA2.dig as structural Verilog
module ULA2 (
  input  [31:0] a,
  input  [31:0] b,
  input  [2:0] f,
  output [31:0] S,
  output over
);

  wire comparator_1_lt;
  wire [31:0] add_1_s, and_1_out, mul_1_mul, mul_1_mul_2, multiplexer_1_out, multiplexer_3_out, not_1_out,
       not_2_out, or_1_out, sub_s, xor_1_out;

  assign or_1_out = b | a;  // Or or_1, 32 bits wide
  assign xor_1_out = b ^ a;  // XOr xor_1, 32 bits wide
  assign and_1_out = b & a;  // And and_1, 32 bits wide
  assign not_1_out = ~a;  // Not not_1, 32 bits wide
  Mul #(.Bits(32)) mul_1 (.a(a), .b(b), .mul({mul_1_mul_2, mul_1_mul}));
  Multiplexer #(.Bits(32)) multiplexer_1 (.sel(1'b0), .in_0(mul_1_mul), .in_1(mul_1_mul_2), .out(multiplexer_1_out));
  Multiplexer #(.Selector_Bits(3), .Bits(32)) multiplexer_2 (
    .sel(f), .in_0(add_1_s), .in_1(sub_s), .in_2(multiplexer_1_out), .in_3(and_1_out), .in_4(or_1_out),
    .in_5(xor_1_out), .in_6(multiplexer_3_out), .in_7(not_1_out), .out(S));
  Comparator #(.Bits(32)) comparator_1 (.a(a), .b(b), .lt(comparator_1_lt));  // open: gt, eq
  Multiplexer #(.Bits(32)) multiplexer_3 (
    .sel(comparator_1_lt), .in_0({32{1'b0}}), .in_1(32'h1), .out(multiplexer_3_out));
  Add #(.Bits(32)) add_1 (.a(a), .b(b), .c_i(1'b0), .s(add_1_s), .c_o(over));
  assign not_2_out = ~b;  // Not not_2, 32 bits wide
  Add #(.Bits(32)) sub (.a(a), .b(not_2_out), .c_i(1'b1), .s(sub_s));  // open: c_o
endmodule
